# Fritzing sketch electrical-input-inverter-3-3v_v2.1 (saved by Fritzing 1.0.7)
circuit board: 6.50816cm x 4.64342cm
perfboards: 1

parts:
  BS170 = NPN-Transistor [package="TO92 [THT]"]
  R1 = Resistor [tolerance=±5% power=0.25W resistance=10k package=THT]
  R2 = Resistor [tolerance=±5% power=0.25W resistance=10k package=THT]
  P1_5V = female pin header, 1 pin [form="♀ (female)"]
  P1_RST = female pin header, 1 pin [form="♀ (female)"]
  P1_Data = female pin header, 1 pin [form="♀ (female)"]
  5V_JP = female pin header, 2 pins [form="♀ (female)"]
  P1_GND = female pin header, 1 pin [form="♀ (female)"]
  P1_NC = female pin header, 1 pin [form="♀ (female)"]  # not connected
  P1_GND' = female pin header, 1 pin [form="♀ (female)"]
  TX = LED - 5mm [color="Red (633nm)" current=0.030A package="5 mm [THT]"]
  R3 = Resistor [tolerance=±5% power=0.25W resistance=220 package=THT]
  DHT_Sensor = female pin header, 4 pins [form="♀ (female)"]
  RPullUpDHT = Resistor [tolerance=±5% power=0.25W resistance=10k package=THT]
  U1 = Heltec CubeCell 1/2AA Node (HTCC-AB02A) [part_number=HTCC-AB02A]

nets:
  N1: BS170.E, P1_GND.pin1, P1_GND'.pin1, TX.anode
  N2: BS170.B, R2.Pin_1, P1_Data.pin1
  N3: BS170.C, R1.Pin_1, U1.pin_4
  N4: R1.Pin_0, R2.Pin_0
  P1 5V/P1 D_Request: P1_5V.pin1, P1_RST.pin1, 5V_JP.pin2
  N5: 5V_JP.pin1, U1.pin_1
  N6: TX.cathode, R3.Pin_1
  N7: R3.Pin_0, U1.pin_31
  N8: DHT_Sensor.pin1, U1.pin_20
  N9: DHT_Sensor.pin3, RPullUpDHT.Pin_1
  N10: DHT_Sensor.pin4, RPullUpDHT.Pin_0, U1.pin_3, U1.pin_21

notes:
  SIGNAL
  10K
  220
  NC
  GND
  VCC
  P1 meter LoRaWAN
  2026.04 V2
  M. Charlier
  WayWayWay

custom parts:
  Heltec CubeCell 1/2AA Node (HTCC-AB02A): Heltec CubeCell HTCC-AB02A 1/2AA LoRaWAN node with ASR6501 processor and SX1262 RF transceiver, featuring 36 pins including SPI, I2C, UART, ADC, PWM, and LoRa radio connections.
