# Fritzing sketch p1-meter-lorawan-v2.1 (saved by Fritzing 1.0.7)
circuit board: 5.85644cm x 4.37857cm
perfboards: 1

parts:
  BS170 = NPN-Transistor [package="TO92 [THT]"]
  R1 = Resistor [tolerance=±5% power=0.25W resistance=10k package=THT]
  R2 = Resistor [tolerance=±5% power=0.25W resistance=10k package=THT]
  +5V = female pin header, 1 pin [form="♀ (female)"]
  RST = female pin header, 1 pin [form="♀ (female)"]
  Data = female pin header, 1 pin [form="♀ (female)"]
  5V_JP = female pin header, 2 pins [form="♀ (female)"]
  GND = female pin header, 1 pin [form="♀ (female)"]
  TX = LED - 5mm [color="Red (633nm)" current=0.030A package="5 mm [THT]"]
  R3 = Resistor [tolerance=±5% power=0.25W resistance=220 package=THT]
  DHT_Sensor = female pin header, 4 pins [form="♀ (female)"]
  RPullUpDHT = Resistor [tolerance=±5% power=0.25W resistance=10k package=THT]
  U1 = Heltec CubeCell 1/2AA Node (HTCC-AB02A) [part_number=HTCC-AB02A]

nets:
  N1: BS170.E, GND.pin1, TX.anode, DHT_Sensor.pin1, U1.pin_2, U1.pin_20
  N2: BS170.B, R2.Pin_1, Data.pin1
  N3: BS170.C, R1.Pin_1, U1.pin_4
  N4: R1.Pin_0, R2.Pin_0, U1.pin_6
  P1 5V/P1 D_Request: +5V.pin1, RST.pin1, 5V_JP.pin2
  N5: 5V_JP.pin1, U1.pin_1
  N6: TX.cathode, R3.Pin_1
  N7: R3.Pin_0, U1.pin_31
  N8: DHT_Sensor.pin3, RPullUpDHT.Pin_1, U1.pin_8
  N9: DHT_Sensor.pin4, RPullUpDHT.Pin_0, U1.pin_3, U1.pin_21

notes:
  SIGNAL
  10K
  220
  NC
  GND
  VCC
  P1 meter LoRaWAN
  2026.06 V2.1
  M. Charlier
  WayWayWay
  P1 meter

custom parts:
  Heltec CubeCell 1/2AA Node (HTCC-AB02A): Heltec CubeCell HTCC-AB02A 1/2AA LoRaWAN node with ASR6501 processor and SX1262 RF transceiver, featuring 36 pins including SPI, I2C, UART, ADC, PWM, and LoRa radio connections.
